# Fritzing sketch schematic (saved by Fritzing 0.9.4)

parts:
  Part1 = TFT 1.8 inch 160x128 w microSD [part_number=358]
  Part2 = Arduino Nano 33 BLE Sense

nets:
  N1: Part1.LITE, Part2.VIN
  N2: Part1.MISO, Part2.D12~/MISO
  N3: Part1.SCLK, Part2.A0
  N4: Part1.MOSI, Part2.D11/MOSI
  N5: Part1.TFTCS, Part2.D10~
  N6: Part1.CARDCS, Part2.D4
  N7: Part1.TFTDC, Part2.D8
  N8: Part1.RESET, Part2.D9~
  GND: Part1.GND, Part2.RESET, Part2.GND, Part2.A7

custom parts:
  TFT 1.8 inch 160x128 w microSD: This lovely little display breakout is the best way to add a small, colorful and bright display to any project. Since the display uses 4-wire SPI to communicate and has its own pixel-addressable frame buffer, it can be used with every kind of microcontroller. Even a very small one with low memory and few pins available! The 1.8" display has 128x160 color pixels.
  Arduino Nano 33 BLE Sense: The Nano 33 BLE Sense (without headers) is Arduino’s 3.3V AI enabled board in the smallest available form factor: 45x18mm! The Arduino Nano 33 BLE Sense is a completely new board on a well-known form factor. It comes with a series of embedded sensors: 9 axis inertial sensor: what makes this board ideal for wearable devices humidity, and temperature sensor: to get highly accurate measurements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
